# Fritzing sketch OLED_IR_WIRING (saved by Fritzing 0.9.3b)

parts:
  Grove1 = Grove OLED 128x96
  U1 = ESP32S-HiLetgo [part_number=ESP32S-HiLetgo]
  M1 = fc-51 [package=THT]

nets:
  GND: Grove1.GND, U1.GND, M1.pin2
  VCC: Grove1.VCC, U1.VIN
  N1: Grove1.SDA, U1.GPIO21
  N2: Grove1.SCL, U1.GPIO22
  N3: U1.3.3, M1.pin3
  N4: U1.GPIO34, M1.pin1

custom parts:
  ESP32S-HiLetgo: HiLetgo ESP-WROOM-32 ESP32 ESP-32S Development Board 2.4GHz Dual-Mode WiFi + Bluetooth Dual Cores Microcontroller The ESP32 integrated with Antenna switches, RF Balun, power amplifiers, low-noise amplifiers, filters, and management modules, and the entire solution occupies the least area of PCB. 2.4 GHz Wi-Fi plus Bluetooth dual-mode chip, with TSMC Ultra-low power consumption 40nm technology,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
  fc-51: Fc-51 Infrared Obstacle Avoidance Proximity Sensor module. IR transmitter led, receiver LED, lm393 compaitor and a pot. 3.3 V to 5V power.
